// Logisim project ALU.circ as structural Verilog: 1 circuit, main circuit main
module main (
  input  [31:0] A,
  input  [31:0] B,
  input  [3:0] Operation,
  input  [4:0] Shamt,
  output [31:0] S,
  output Zero
);

  wire Slt1bit, Sltu1bit;
  wire [31:0] A_ND, Add, O_R, S_ll, S_rl, Slt, Sltu, Sub;

  Adder #(.width(32)) adder_1 (.a(A), .b(B), .out(Add));  // open: cin, cout
  Comparator #(.width(32)) comparator_1 (.a(A), .b(B), .lt(Slt1bit));  // open: gt, eq
  assign Slt = {{31{Slt1bit}}, Slt1bit};  // Bit_Extender bit_extender_1
  Shifter #(.width(32)) shifter_1 (.in(A), .\dist (Shamt), .out(S_ll));
  Subtractor #(.width(32)) subtractor_1 (.a(A), .b(B), .out(Sub));  // open: bin, bout
  Comparator #(.mode("unsigned"), .width(32)) comparator_2 (.a(A), .b(B), .lt(Sltu1bit));  // open: gt, eq
  assign Sltu = {{31{1'b0}}, Sltu1bit};  // Bit_Extender bit_extender_2
  Shifter #(.shift("lr"), .width(32)) shifter_2 (.in(A), .\dist (Shamt), .out(S_rl));
  Multiplexer #(.select(4), .width(32)) multiplexer_1 (
    .in0(Add), .in1(Sub), .in2(Slt), .in3(Sltu), .in4(A_ND), .in5(O_R), .in6(S_ll), .in7(S_rl), .out(S),
    .sel(Operation));  // open: in8, in9, in10, in11, in12, in13, in14, in15
  assign A_ND = A & B;  // AND_Gate and_1, 32 bits wide
  assign O_R = A | B;  // OR_Gate or_1, 32 bits wide
  Comparator #(.width(32)) comparator_3 (.a(S), .b({32{1'b0}}), .eq(Zero));  // open: gt, lt

  // Other names for the same wires on the sheet: O_UT[31:0] = S; Selector[3:0] = Operation

  // Notes on the sheet:
  //   Inputs
  //   Arithmetic
  //   Logic
  //   Ouputs
  //   Zero
endmodule
