// Logisim project RF.circ as structural Verilog: 1 circuit, main circuit main
module main (
  input  [31:0] DataInput,
  input  Reset,
  input  R_W,
  input  Clock,
  input  [4:0] DataAddress,
  input  [4:0] SelectorA,
  input  [4:0] SelectorB,
  output [31:0] A,
  output [31:0] B
);

  wire L0, L1, L2, L3, L4, L5, L6, L7, L8, L9, L10, L11, L12, L13, L14, L15, L16, L17, L18, L19, L20, L21,
       L22, L23, L24, L25, L26, L27, L28, L29, L30, L31;
  wire [31:0] Q0, Q1, Q2, Q3, Q4, Q5, Q6, Q7, Q8, Q9, Q10, Q11, Q12, Q13, Q14, Q15, Q16, Q17, Q18, Q19, Q20,
       Q21, Q22, Q23, Q24, Q25, Q26, Q27, Q28, Q29, Q30, Q31;

  Decoder #(.select(5)) decoder_1 (
    .out0(L0), .out1(L1), .out2(L2), .out3(L3), .out4(L4), .out5(L5), .out6(L6), .out7(L7), .out8(L8),
    .out9(L9), .out10(L10), .out11(L11), .out12(L12), .out13(L13), .out14(L14), .out15(L15), .out16(L16),
    .out17(L17), .out18(L18), .out19(L19), .out20(L20), .out21(L21), .out22(L22), .out23(L23), .out24(L24),
    .out25(L25), .out26(L26), .out27(L27), .out28(L28), .out29(L29), .out30(L30), .out31(L31),
    .sel(DataAddress), .en(R_W));
  Register #(.width(32)) register_1 (.D(DataInput), .en(L0), .clk(Clock), .Q(Q0), .clr(Reset));
  Register #(.width(32)) register_2 (.D(DataInput), .en(L1), .clk(Clock), .Q(Q1), .clr(Reset));
  Register #(.width(32)) register_3 (.D(DataInput), .en(L2), .clk(Clock), .Q(Q2), .clr(Reset));
  Register #(.width(32)) register_4 (.D(DataInput), .en(L3), .clk(Clock), .Q(Q3), .clr(Reset));
  Register #(.width(32)) register_5 (.D(DataInput), .en(L4), .clk(Clock), .Q(Q4), .clr(Reset));
  Register #(.width(32)) register_6 (.D(DataInput), .en(L5), .clk(Clock), .Q(Q5), .clr(Reset));
  Register #(.width(32)) register_7 (.D(DataInput), .en(L6), .clk(Clock), .Q(Q6), .clr(Reset));
  Register #(.width(32)) register_8 (.D(DataInput), .en(L7), .clk(Clock), .Q(Q7), .clr(Reset));
  Multiplexer #(.select(5), .width(32)) multiplexer_1 (
    .in0(Q0), .in1(Q1), .in2(Q2), .in3(Q3), .in4(Q4), .in5(Q5), .in6(Q6), .in7(Q7), .in8(Q8), .in9(Q9),
    .in10(Q10), .in11(Q11), .in12(Q12), .in13(Q13), .in14(Q14), .in15(Q15), .in16(Q16), .in17(Q17),
    .in18(Q18), .in19(Q19), .in20(Q20), .in21(Q21), .in22(Q22), .in23(Q23), .in24(Q24), .in25(Q25),
    .in26(Q26), .in27(Q27), .in28(Q28), .in29(Q29), .in30(Q30), .in31(Q31), .out(A), .sel(SelectorA));
  Register #(.width(32)) register_9 (.D(DataInput), .en(L8), .clk(Clock), .Q(Q8), .clr(Reset));
  Register #(.width(32)) register_10 (.D(DataInput), .en(L9), .clk(Clock), .Q(Q9), .clr(Reset));
  Register #(.width(32)) register_11 (.D(DataInput), .en(L10), .clk(Clock), .Q(Q10), .clr(Reset));
  Register #(.width(32)) register_12 (.D(DataInput), .en(L11), .clk(Clock), .Q(Q11), .clr(Reset));
  Register #(.width(32)) register_13 (.D(DataInput), .en(L12), .clk(Clock), .Q(Q12), .clr(Reset));
  Register #(.width(32)) register_14 (.D(DataInput), .en(L13), .clk(Clock), .Q(Q13), .clr(Reset));
  Register #(.width(32)) register_15 (.D(DataInput), .en(L14), .clk(Clock), .Q(Q14), .clr(Reset));
  Register #(.width(32)) register_16 (.D(DataInput), .en(L15), .clk(Clock), .Q(Q15), .clr(Reset));
  Register #(.width(32)) register_17 (.D(DataInput), .en(L16), .clk(Clock), .Q(Q16), .clr(Reset));
  Register #(.width(32)) register_18 (.D(DataInput), .en(L17), .clk(Clock), .Q(Q17), .clr(Reset));
  Register #(.width(32)) register_19 (.D(DataInput), .en(L18), .clk(Clock), .Q(Q18), .clr(Reset));
  Register #(.width(32)) register_20 (.D(DataInput), .en(L19), .clk(Clock), .Q(Q19), .clr(Reset));
  Register #(.width(32)) register_21 (.D(DataInput), .en(L20), .clk(Clock), .Q(Q20), .clr(Reset));
  Register #(.width(32)) register_22 (.D(DataInput), .en(L21), .clk(Clock), .Q(Q21), .clr(Reset));
  Register #(.width(32)) register_23 (.D(DataInput), .en(L22), .clk(Clock), .Q(Q22), .clr(Reset));
  Register #(.width(32)) register_24 (.D(DataInput), .en(L23), .clk(Clock), .Q(Q23), .clr(Reset));
  Multiplexer #(.select(5), .width(32)) multiplexer_2 (
    .in0(Q0), .in1(Q1), .in2(Q2), .in3(Q3), .in4(Q4), .in5(Q5), .in6(Q6), .in7(Q7), .in8(Q8), .in9(Q9),
    .in10(Q10), .in11(Q11), .in12(Q12), .in13(Q13), .in14(Q14), .in15(Q15), .in16(Q16), .in17(Q17),
    .in18(Q18), .in19(Q19), .in20(Q20), .in21(Q21), .in22(Q22), .in23(Q23), .in24(Q24), .in25(Q25),
    .in26(Q26), .in27(Q27), .in28(Q28), .in29(Q29), .in30(Q30), .in31(Q31), .out(B), .sel(SelectorB));
  Register #(.width(32)) register_25 (.D(DataInput), .en(L24), .clk(Clock), .Q(Q24), .clr(Reset));
  Register #(.width(32)) register_26 (.D(DataInput), .en(L25), .clk(Clock), .Q(Q25), .clr(Reset));
  Register #(.width(32)) register_27 (.D(DataInput), .en(L26), .clk(Clock), .Q(Q26), .clr(Reset));
  Register #(.width(32)) register_28 (.D(DataInput), .en(L27), .clk(Clock), .Q(Q27), .clr(Reset));
  Register #(.width(32)) register_29 (.D(DataInput), .en(L28), .clk(Clock), .Q(Q28), .clr(Reset));
  Register #(.width(32)) register_30 (.D(DataInput), .en(L29), .clk(Clock), .Q(Q29), .clr(Reset));
  Register #(.width(32)) register_31 (.D(DataInput), .en(L30), .clk(Clock), .Q(Q30), .clr(Reset));
  Register #(.width(32)) register_32 (.D(DataInput), .en(L31), .clk(Clock), .Q(Q31), .clr(Reset));

  // Other names for the same wires on the sheet: Clk = Clock; DA[4:0] = DataAddress; DI[31:0] = DataInput; R = Reset;
  //   SA[4:0] = SelectorA; SB[4:0] = SelectorB

  // Notes on the sheet:
  //   Input
  //   Output
endmodule
